// Logisim project final.circ as structural Verilog: 18 circuits, main circuit display led
module display_led (
  output out_1,
  output out_2
);

  wire and_1_out, button_1_out, button_2_out, button_3_out, button_4_out, button_5_out, button_6_out,
       button_7_out, button_8_out, button_9_out, button_10_out_11, button_10_out_12, button_10_out_13,
       button_10_out_14, button_10_out_15, button_10_out_16, button_10_out_17, button_10_out_18,
       button_10_out_19, CLEAR_out, CLEAR_SAVED_PATTERN_out, clock_1_out, display_encode_1_out_11,
       display_encode_1_out_12, display_encode_1_out_13, display_encode_1_out_14, display_encode_1_out_15,
       display_encode_1_out_16, display_encode_1_out_17, display_encode_1_out_18, display_encode_1_out_19,
       momentary_1_out_2, or_1_out, SET_PATTERN_out, stay_1_out_3, stay_2_out_3, UNLOCK_out;
  wire [6:0] letter_display_sub2_1_out_3;
  wire [8:0] led1_1__0, led1_1__1, led1_1__2, led1_1__3, led1_1__4, led1_1__5, led1_1__6, led1_1__7,
       led1_1__8, led1_2__0, led1_2__1, led1_2__2, led1_2__3, led1_2__4, led1_2__5, led1_2__6, led1_2__7,
       led1_2__8, led1_3__0, led1_3__1, led1_3__2, led1_3__3, led1_3__4, led1_3__5, led1_3__6, led1_3__7,
       led1_3__8, led1_4__0, led1_4__1, led1_4__2, led1_4__3, led1_4__4, led1_4__5, led1_4__6, led1_4__7,
       led1_4__8;

  DotMatrix #(.matrixcols(9), .matrixrows(9)) dotmatrix_1 (
    .col0(led1_3__0), .col1(led1_3__1), .col2(led1_3__2), .col3(led1_3__3), .col4(led1_3__4),
    .col5(led1_3__5), .col6(led1_3__6), .col7(led1_3__7), .col8(led1_3__8));
  DotMatrix #(.matrixcols(9), .matrixrows(9)) dotmatrix_2 (
    .col0(led1_1__0), .col1(led1_1__1), .col2(led1_1__2), .col3(led1_1__3), .col4(led1_1__4),
    .col5(led1_1__5), .col6(led1_1__6), .col7(led1_1__7), .col8(led1_1__8));
  led1 led1_1 (
    ._3(led1_1__3), ._2(led1_1__2), ._1(led1_1__1), ._0(led1_1__0), .in_2(display_encode_1_out_15),
    .in_4(display_encode_1_out_18), .CLEAR(or_1_out), ._4(led1_1__4), ._5(led1_1__5), ._6(led1_1__6),
    ._7(led1_1__7), ._8(led1_1__8), .in_1(display_encode_1_out_14), .in_3(display_encode_1_out_17));
  DotMatrix #(.matrixcols(9), .matrixrows(9)) dotmatrix_3 (
    .col0(led1_4__0), .col1(led1_4__1), .col2(led1_4__2), .col3(led1_4__3), .col4(led1_4__4),
    .col5(led1_4__5), .col6(led1_4__6), .col7(led1_4__7), .col8(led1_4__8));
  DotMatrix #(.matrixcols(9), .matrixrows(9)) dotmatrix_4 (
    .col0(led1_2__0), .col1(led1_2__1), .col2(led1_2__2), .col3(led1_2__3), .col4(led1_2__4),
    .col5(led1_2__5), .col6(led1_2__6), .col7(led1_2__7), .col8(led1_2__8));
  led1 led1_2 (
    ._3(led1_2__3), ._2(led1_2__2), ._1(led1_2__1), ._0(led1_2__0), .in_2(display_encode_1_out_16),
    .in_4(display_encode_1_out_19), .CLEAR(or_1_out), ._4(led1_2__4), ._5(led1_2__5), ._6(led1_2__6),
    ._7(led1_2__7), ._8(led1_2__8), .in_1(display_encode_1_out_15), .in_3(display_encode_1_out_18));
  led1 led1_3 (
    ._3(led1_3__3), ._2(led1_3__2), ._1(led1_3__1), ._0(led1_3__0), .in_2(display_encode_1_out_12),
    .in_4(display_encode_1_out_15), .CLEAR(or_1_out), ._4(led1_3__4), ._5(led1_3__5), ._6(led1_3__6),
    ._7(led1_3__7), ._8(led1_3__8), .in_1(display_encode_1_out_11), .in_3(display_encode_1_out_14));
  led1 led1_4 (
    ._3(led1_4__3), ._2(led1_4__2), ._1(led1_4__1), ._0(led1_4__0), .in_2(display_encode_1_out_13),
    .in_4(display_encode_1_out_16), .CLEAR(or_1_out), ._4(led1_4__4), ._5(led1_4__5), ._6(led1_4__6),
    ._7(led1_4__7), ._8(led1_4__8), .in_1(display_encode_1_out_12), .in_3(display_encode_1_out_15));
  Clock clock_1 (.out(clock_1_out));
  TTY #(.cols(20)) tty_1 (.data(letter_display_sub2_1_out_3), .clk(clock_1_out), .we(1'b1), .clr(momentary_1_out_2));
  or or_1 (or_1_out, CLEAR_out, CLEAR_SAVED_PATTERN_out);
  Button CLEAR_SAVED_PATTERN (.out(CLEAR_SAVED_PATTERN_out));
  Button SET_PATTERN (.out(SET_PATTERN_out));
  Button UNLOCK (.out(UNLOCK_out));
  Button CLEAR (.out(CLEAR_out));
  Button button_1 (.out(button_1_out));
  Button button_2 (.out(button_2_out));
  Button button_3 (.out(button_3_out));
  momentary momentary_1 (.in_1(out_1), .out_2(momentary_1_out_2));
  Button button_4 (.out(button_4_out));
  Button button_5 (.out(button_5_out));
  Button button_6 (.out(button_6_out));
  stay stay_1 (.in_1(UNLOCK_out), .CLEAR(or_1_out), .out_3(stay_1_out_3));
  stay stay_2 (.in_1(SET_PATTERN_out), .CLEAR(or_1_out), .out_3(stay_2_out_3));
  letter_display_sub2 letter_display_sub2_1 (
    .MOMENTARY_IP(momentary_1_out_2), .NORMAL_IP(out_1), .out_3(letter_display_sub2_1_out_3));
  Button button_7 (.out(button_7_out));
  Button button_8 (.out(button_8_out));
  Button button_9 (.out(button_9_out));
  and and_1 (and_1_out, CLEAR_SAVED_PATTERN_out, out_1);
  button button_10 (
    .CLEAR(or_1_out), .in_2(button_1_out), .in_3(button_4_out), .in_4(button_7_out), .in_5(button_2_out),
    .in_6(button_5_out), .in_7(button_8_out), .in_8(button_3_out), .in_9(button_6_out), .in_10(button_9_out),
    .out_11(button_10_out_11), .out_12(button_10_out_12), .out_13(button_10_out_13),
    .out_14(button_10_out_14), .out_15(button_10_out_15), .out_16(button_10_out_16),
    .out_17(button_10_out_17), .out_18(button_10_out_18), .out_19(button_10_out_19));
  Compare compare_1 (
    .UNLOCK(stay_1_out_3), .RESET(stay_2_out_3), .RESET_CLR(and_1_out), .in_4(button_10_out_11),
    .in_5(button_10_out_12), .in_6(button_10_out_13), .in_7(button_10_out_14), .in_8(button_10_out_15),
    .in_9(button_10_out_16), .in_10(button_10_out_17), .in_11(button_10_out_18), .in_12(button_10_out_19),
    .NORMAL_CLR(or_1_out), .out_14(out_1));
  display_encode display_encode_1 (
    .in_1(button_10_out_11), .in_2(button_10_out_12), .in_3(button_10_out_13), .in_4(button_10_out_14),
    .in_5(button_10_out_15), .in_6(button_10_out_16), .in_7(button_10_out_17), .in_8(button_10_out_18),
    .in_9(button_10_out_19), .CLEAR(or_1_out), .out_11(display_encode_1_out_11),
    .out_12(display_encode_1_out_12), .out_13(display_encode_1_out_13), .out_14(display_encode_1_out_14),
    .out_15(display_encode_1_out_15), .out_16(display_encode_1_out_16), .out_17(display_encode_1_out_17),
    .out_18(display_encode_1_out_18), .out_19(display_encode_1_out_19));
endmodule

module Save_Inputs (
  input  in_1,
  input  in_2,
  input  in_3,
  input  in_4,
  input  in_5,
  input  in_6,
  input  in_7,
  input  in_8,
  input  in_9,
  input  CLEAR,
  output out_11,
  output out_12,
  output out_13,
  output out_14,
  output out_15,
  output out_16,
  output out_17,
  output out_18,
  output out_19,
  output out_20,
  output out_21,
  output out_22,
  output out_23,
  output out_24,
  output out_25,
  output out_26,
  output out_27,
  output out_28,
  output out_29,
  output out_30,
  output out_31,
  output out_32,
  output out_33,
  output out_34,
  output out_35,
  output out_36,
  output out_37,
  output out_38,
  output out_39,
  output out_40,
  output out_41,
  output out_42,
  output out_43,
  output out_44,
  output out_45,
  output out_46,
  output out_47,
  output out_48,
  output out_49,
  output out_50,
  output out_51,
  output out_52,
  output out_53,
  output out_54,
  output out_55,
  output out_56,
  output out_57,
  output out_58,
  output out_59,
  output out_60,
  output out_61,
  output out_62,
  output out_63,
  output out_64,
  output out_65,
  output out_66,
  output out_67,
  output out_68,
  output out_69,
  output out_70,
  output out_71,
  output out_72,
  output out_73,
  output out_74,
  output out_75,
  output out_76,
  output out_77,
  output out_78,
  output out_79,
  output out_80,
  output out_81,
  output out_82,
  output out_83,
  output out_84,
  output out_85,
  output out_86,
  output out_87,
  output out_88,
  output out_89,
  output out_90,
  output out_91
);

  wire save_ip_sub_1_1_out_21, save_ip_sub_1_2_out_21, save_ip_sub_1_3_out_21, save_ip_sub_1_4_out_21,
       save_ip_sub_1_5_out_21, save_ip_sub_1_6_out_21, save_ip_sub_1_7_out_21, save_ip_sub_1_8_out_21,
       save_ip_sub_2_1_out_19, save_ip_sub_2_1_out_20, save_ip_sub_2_1_out_21, save_ip_sub_2_1_out_22,
       save_ip_sub_2_1_out_23, save_ip_sub_2_1_out_24, save_ip_sub_2_1_out_25, save_ip_sub_2_1_out_26,
       save_ip_sub_2_1_out_27, save_ip_sub_2_2_out_19, save_ip_sub_2_2_out_20, save_ip_sub_2_2_out_21,
       save_ip_sub_2_2_out_22, save_ip_sub_2_2_out_23, save_ip_sub_2_2_out_24, save_ip_sub_2_2_out_25,
       save_ip_sub_2_2_out_26, save_ip_sub_2_2_out_27, save_ip_sub_2_3_out_19, save_ip_sub_2_3_out_20,
       save_ip_sub_2_3_out_21, save_ip_sub_2_3_out_22, save_ip_sub_2_3_out_23, save_ip_sub_2_3_out_24,
       save_ip_sub_2_3_out_25, save_ip_sub_2_3_out_26, save_ip_sub_2_3_out_27, save_ip_sub_2_4_out_19,
       save_ip_sub_2_4_out_20, save_ip_sub_2_4_out_21, save_ip_sub_2_4_out_22, save_ip_sub_2_4_out_23,
       save_ip_sub_2_4_out_24, save_ip_sub_2_4_out_25, save_ip_sub_2_4_out_26, save_ip_sub_2_4_out_27,
       save_ip_sub_2_5_out_19, save_ip_sub_2_5_out_20, save_ip_sub_2_5_out_21, save_ip_sub_2_5_out_22,
       save_ip_sub_2_5_out_23, save_ip_sub_2_5_out_24, save_ip_sub_2_5_out_25, save_ip_sub_2_5_out_26,
       save_ip_sub_2_5_out_27, save_ip_sub_2_6_out_19, save_ip_sub_2_6_out_20, save_ip_sub_2_6_out_21,
       save_ip_sub_2_6_out_22, save_ip_sub_2_6_out_23, save_ip_sub_2_6_out_24, save_ip_sub_2_6_out_25,
       save_ip_sub_2_6_out_26, save_ip_sub_2_6_out_27, save_ip_sub_2_7_out_19, save_ip_sub_2_7_out_20,
       save_ip_sub_2_7_out_21, save_ip_sub_2_7_out_22, save_ip_sub_2_7_out_23, save_ip_sub_2_7_out_24,
       save_ip_sub_2_7_out_25, save_ip_sub_2_7_out_26, save_ip_sub_2_7_out_27, save_ip_sub_2_8_out_19,
       save_ip_sub_2_8_out_20, save_ip_sub_2_8_out_21, save_ip_sub_2_8_out_22, save_ip_sub_2_8_out_23,
       save_ip_sub_2_8_out_24, save_ip_sub_2_8_out_25, save_ip_sub_2_8_out_26, save_ip_sub_2_8_out_27;

  save_ip_sub_1 save_ip_sub_1_1 (
    .in_1(1'b1), .in_2(in_1), .in_3(in_2), .in_4(in_3), .in_5(in_4), .in_6(in_5), .in_7(in_6), .in_8(in_7),
    .in_9(in_8), .in_10(in_9), .CLEAR(CLEAR), .out_12(out_11), .out_13(out_12), .out_14(out_13),
    .out_15(out_14), .out_16(out_15), .out_17(out_16), .out_18(out_17), .out_19(out_19), .out_20(out_21),
    .out_21(save_ip_sub_1_1_out_21));
  save_ip_sub_2 save_ip_sub_2_1 (
    .in_10(in_1), .in_11(in_2), .in_12(in_3), .in_13(in_4), .in_14(in_5), .in_15(in_6), .in_16(in_7),
    .in_17(in_8), .in_18(in_9), .in_1(out_11), .in_2(out_12), .in_3(out_13), .in_4(out_14), .in_5(out_15),
    .in_6(out_16), .in_7(out_17), .in_8(out_19), .in_9(out_21), .out_19(save_ip_sub_2_1_out_19),
    .out_20(save_ip_sub_2_1_out_20), .out_21(save_ip_sub_2_1_out_21), .out_22(save_ip_sub_2_1_out_22),
    .out_23(save_ip_sub_2_1_out_23), .out_24(save_ip_sub_2_1_out_24), .out_25(save_ip_sub_2_1_out_25),
    .out_26(save_ip_sub_2_1_out_26), .out_27(save_ip_sub_2_1_out_27));
  save_ip_sub_1 save_ip_sub_1_2 (
    .in_1(save_ip_sub_1_1_out_21), .in_2(save_ip_sub_2_1_out_19), .in_3(save_ip_sub_2_1_out_20),
    .in_4(save_ip_sub_2_1_out_21), .in_5(save_ip_sub_2_1_out_22), .in_6(save_ip_sub_2_1_out_23),
    .in_7(save_ip_sub_2_1_out_24), .in_8(save_ip_sub_2_1_out_25), .in_9(save_ip_sub_2_1_out_26),
    .in_10(save_ip_sub_2_1_out_27), .CLEAR(CLEAR), .out_12(out_18), .out_13(out_20), .out_14(out_22),
    .out_15(out_23), .out_16(out_24), .out_17(out_25), .out_18(out_26), .out_19(out_28), .out_20(out_30),
    .out_21(save_ip_sub_1_2_out_21));
  save_ip_sub_2 save_ip_sub_2_2 (
    .in_10(save_ip_sub_2_1_out_19), .in_11(save_ip_sub_2_1_out_20), .in_12(save_ip_sub_2_1_out_21),
    .in_13(save_ip_sub_2_1_out_22), .in_14(save_ip_sub_2_1_out_23), .in_15(save_ip_sub_2_1_out_24),
    .in_16(save_ip_sub_2_1_out_25), .in_17(save_ip_sub_2_1_out_26), .in_18(save_ip_sub_2_1_out_27),
    .in_1(out_18), .in_2(out_20), .in_3(out_22), .in_4(out_23), .in_5(out_24), .in_6(out_25), .in_7(out_26),
    .in_8(out_28), .in_9(out_30), .out_19(save_ip_sub_2_2_out_19), .out_20(save_ip_sub_2_2_out_20),
    .out_21(save_ip_sub_2_2_out_21), .out_22(save_ip_sub_2_2_out_22), .out_23(save_ip_sub_2_2_out_23),
    .out_24(save_ip_sub_2_2_out_24), .out_25(save_ip_sub_2_2_out_25), .out_26(save_ip_sub_2_2_out_26),
    .out_27(save_ip_sub_2_2_out_27));
  save_ip_sub_1 save_ip_sub_1_3 (
    .in_1(save_ip_sub_1_2_out_21), .in_2(save_ip_sub_2_2_out_19), .in_3(save_ip_sub_2_2_out_20),
    .in_4(save_ip_sub_2_2_out_21), .in_5(save_ip_sub_2_2_out_22), .in_6(save_ip_sub_2_2_out_23),
    .in_7(save_ip_sub_2_2_out_24), .in_8(save_ip_sub_2_2_out_25), .in_9(save_ip_sub_2_2_out_26),
    .in_10(save_ip_sub_2_2_out_27), .CLEAR(CLEAR), .out_12(out_27), .out_13(out_29), .out_14(out_31),
    .out_15(out_32), .out_16(out_33), .out_17(out_34), .out_18(out_35), .out_19(out_37), .out_20(out_39),
    .out_21(save_ip_sub_1_3_out_21));
  save_ip_sub_2 save_ip_sub_2_3 (
    .in_10(save_ip_sub_2_2_out_19), .in_11(save_ip_sub_2_2_out_20), .in_12(save_ip_sub_2_2_out_21),
    .in_13(save_ip_sub_2_2_out_22), .in_14(save_ip_sub_2_2_out_23), .in_15(save_ip_sub_2_2_out_24),
    .in_16(save_ip_sub_2_2_out_25), .in_17(save_ip_sub_2_2_out_26), .in_18(save_ip_sub_2_2_out_27),
    .in_1(out_27), .in_2(out_29), .in_3(out_31), .in_4(out_32), .in_5(out_33), .in_6(out_34), .in_7(out_35),
    .in_8(out_37), .in_9(out_39), .out_19(save_ip_sub_2_3_out_19), .out_20(save_ip_sub_2_3_out_20),
    .out_21(save_ip_sub_2_3_out_21), .out_22(save_ip_sub_2_3_out_22), .out_23(save_ip_sub_2_3_out_23),
    .out_24(save_ip_sub_2_3_out_24), .out_25(save_ip_sub_2_3_out_25), .out_26(save_ip_sub_2_3_out_26),
    .out_27(save_ip_sub_2_3_out_27));
  save_ip_sub_1 save_ip_sub_1_4 (
    .in_1(save_ip_sub_1_3_out_21), .in_2(save_ip_sub_2_3_out_19), .in_3(save_ip_sub_2_3_out_20),
    .in_4(save_ip_sub_2_3_out_21), .in_5(save_ip_sub_2_3_out_22), .in_6(save_ip_sub_2_3_out_23),
    .in_7(save_ip_sub_2_3_out_24), .in_8(save_ip_sub_2_3_out_25), .in_9(save_ip_sub_2_3_out_26),
    .in_10(save_ip_sub_2_3_out_27), .CLEAR(CLEAR), .out_12(out_36), .out_13(out_38), .out_14(out_40),
    .out_15(out_41), .out_16(out_42), .out_17(out_43), .out_18(out_44), .out_19(out_46), .out_20(out_48),
    .out_21(save_ip_sub_1_4_out_21));
  save_ip_sub_2 save_ip_sub_2_4 (
    .in_10(save_ip_sub_2_3_out_19), .in_11(save_ip_sub_2_3_out_20), .in_12(save_ip_sub_2_3_out_21),
    .in_13(save_ip_sub_2_3_out_22), .in_14(save_ip_sub_2_3_out_23), .in_15(save_ip_sub_2_3_out_24),
    .in_16(save_ip_sub_2_3_out_25), .in_17(save_ip_sub_2_3_out_26), .in_18(save_ip_sub_2_3_out_27),
    .in_1(out_36), .in_2(out_38), .in_3(out_40), .in_4(out_41), .in_5(out_42), .in_6(out_43), .in_7(out_44),
    .in_8(out_46), .in_9(out_48), .out_19(save_ip_sub_2_4_out_19), .out_20(save_ip_sub_2_4_out_20),
    .out_21(save_ip_sub_2_4_out_21), .out_22(save_ip_sub_2_4_out_22), .out_23(save_ip_sub_2_4_out_23),
    .out_24(save_ip_sub_2_4_out_24), .out_25(save_ip_sub_2_4_out_25), .out_26(save_ip_sub_2_4_out_26),
    .out_27(save_ip_sub_2_4_out_27));
  save_ip_sub_1 save_ip_sub_1_5 (
    .in_1(save_ip_sub_1_4_out_21), .in_2(save_ip_sub_2_4_out_19), .in_3(save_ip_sub_2_4_out_20),
    .in_4(save_ip_sub_2_4_out_21), .in_5(save_ip_sub_2_4_out_22), .in_6(save_ip_sub_2_4_out_23),
    .in_7(save_ip_sub_2_4_out_24), .in_8(save_ip_sub_2_4_out_25), .in_9(save_ip_sub_2_4_out_26),
    .in_10(save_ip_sub_2_4_out_27), .CLEAR(CLEAR), .out_12(out_45), .out_13(out_47), .out_14(out_49),
    .out_15(out_50), .out_16(out_51), .out_17(out_52), .out_18(out_53), .out_19(out_55), .out_20(out_57),
    .out_21(save_ip_sub_1_5_out_21));
  save_ip_sub_2 save_ip_sub_2_5 (
    .in_10(save_ip_sub_2_4_out_19), .in_11(save_ip_sub_2_4_out_20), .in_12(save_ip_sub_2_4_out_21),
    .in_13(save_ip_sub_2_4_out_22), .in_14(save_ip_sub_2_4_out_23), .in_15(save_ip_sub_2_4_out_24),
    .in_16(save_ip_sub_2_4_out_25), .in_17(save_ip_sub_2_4_out_26), .in_18(save_ip_sub_2_4_out_27),
    .in_1(out_45), .in_2(out_47), .in_3(out_49), .in_4(out_50), .in_5(out_51), .in_6(out_52), .in_7(out_53),
    .in_8(out_55), .in_9(out_57), .out_19(save_ip_sub_2_5_out_19), .out_20(save_ip_sub_2_5_out_20),
    .out_21(save_ip_sub_2_5_out_21), .out_22(save_ip_sub_2_5_out_22), .out_23(save_ip_sub_2_5_out_23),
    .out_24(save_ip_sub_2_5_out_24), .out_25(save_ip_sub_2_5_out_25), .out_26(save_ip_sub_2_5_out_26),
    .out_27(save_ip_sub_2_5_out_27));
  save_ip_sub_1 save_ip_sub_1_6 (
    .in_1(save_ip_sub_1_5_out_21), .in_2(save_ip_sub_2_5_out_19), .in_3(save_ip_sub_2_5_out_20),
    .in_4(save_ip_sub_2_5_out_21), .in_5(save_ip_sub_2_5_out_22), .in_6(save_ip_sub_2_5_out_23),
    .in_7(save_ip_sub_2_5_out_24), .in_8(save_ip_sub_2_5_out_25), .in_9(save_ip_sub_2_5_out_26),
    .in_10(save_ip_sub_2_5_out_27), .CLEAR(CLEAR), .out_12(out_54), .out_13(out_56), .out_14(out_58),
    .out_15(out_59), .out_16(out_60), .out_17(out_61), .out_18(out_62), .out_19(out_64), .out_20(out_66),
    .out_21(save_ip_sub_1_6_out_21));
  save_ip_sub_2 save_ip_sub_2_6 (
    .in_10(save_ip_sub_2_5_out_19), .in_11(save_ip_sub_2_5_out_20), .in_12(save_ip_sub_2_5_out_21),
    .in_13(save_ip_sub_2_5_out_22), .in_14(save_ip_sub_2_5_out_23), .in_15(save_ip_sub_2_5_out_24),
    .in_16(save_ip_sub_2_5_out_25), .in_17(save_ip_sub_2_5_out_26), .in_18(save_ip_sub_2_5_out_27),
    .in_1(out_54), .in_2(out_56), .in_3(out_58), .in_4(out_59), .in_5(out_60), .in_6(out_61), .in_7(out_62),
    .in_8(out_64), .in_9(out_66), .out_19(save_ip_sub_2_6_out_19), .out_20(save_ip_sub_2_6_out_20),
    .out_21(save_ip_sub_2_6_out_21), .out_22(save_ip_sub_2_6_out_22), .out_23(save_ip_sub_2_6_out_23),
    .out_24(save_ip_sub_2_6_out_24), .out_25(save_ip_sub_2_6_out_25), .out_26(save_ip_sub_2_6_out_26),
    .out_27(save_ip_sub_2_6_out_27));
  save_ip_sub_1 save_ip_sub_1_7 (
    .in_1(save_ip_sub_1_6_out_21), .in_2(save_ip_sub_2_6_out_19), .in_3(save_ip_sub_2_6_out_20),
    .in_4(save_ip_sub_2_6_out_21), .in_5(save_ip_sub_2_6_out_22), .in_6(save_ip_sub_2_6_out_23),
    .in_7(save_ip_sub_2_6_out_24), .in_8(save_ip_sub_2_6_out_25), .in_9(save_ip_sub_2_6_out_26),
    .in_10(save_ip_sub_2_6_out_27), .CLEAR(CLEAR), .out_12(out_63), .out_13(out_65), .out_14(out_67),
    .out_15(out_68), .out_16(out_69), .out_17(out_70), .out_18(out_71), .out_19(out_73), .out_20(out_75),
    .out_21(save_ip_sub_1_7_out_21));
  save_ip_sub_2 save_ip_sub_2_7 (
    .in_10(save_ip_sub_2_6_out_19), .in_11(save_ip_sub_2_6_out_20), .in_12(save_ip_sub_2_6_out_21),
    .in_13(save_ip_sub_2_6_out_22), .in_14(save_ip_sub_2_6_out_23), .in_15(save_ip_sub_2_6_out_24),
    .in_16(save_ip_sub_2_6_out_25), .in_17(save_ip_sub_2_6_out_26), .in_18(save_ip_sub_2_6_out_27),
    .in_1(out_63), .in_2(out_65), .in_3(out_67), .in_4(out_68), .in_5(out_69), .in_6(out_70), .in_7(out_71),
    .in_8(out_73), .in_9(out_75), .out_19(save_ip_sub_2_7_out_19), .out_20(save_ip_sub_2_7_out_20),
    .out_21(save_ip_sub_2_7_out_21), .out_22(save_ip_sub_2_7_out_22), .out_23(save_ip_sub_2_7_out_23),
    .out_24(save_ip_sub_2_7_out_24), .out_25(save_ip_sub_2_7_out_25), .out_26(save_ip_sub_2_7_out_26),
    .out_27(save_ip_sub_2_7_out_27));
  save_ip_sub_1 save_ip_sub_1_8 (
    .in_1(save_ip_sub_1_7_out_21), .in_2(save_ip_sub_2_7_out_19), .in_3(save_ip_sub_2_7_out_20),
    .in_4(save_ip_sub_2_7_out_21), .in_5(save_ip_sub_2_7_out_22), .in_6(save_ip_sub_2_7_out_23),
    .in_7(save_ip_sub_2_7_out_24), .in_8(save_ip_sub_2_7_out_25), .in_9(save_ip_sub_2_7_out_26),
    .in_10(save_ip_sub_2_7_out_27), .CLEAR(CLEAR), .out_12(out_72), .out_13(out_74), .out_14(out_76),
    .out_15(out_77), .out_16(out_78), .out_17(out_79), .out_18(out_80), .out_19(out_82), .out_20(out_84),
    .out_21(save_ip_sub_1_8_out_21));
  save_ip_sub_2 save_ip_sub_2_8 (
    .in_10(save_ip_sub_2_7_out_19), .in_11(save_ip_sub_2_7_out_20), .in_12(save_ip_sub_2_7_out_21),
    .in_13(save_ip_sub_2_7_out_22), .in_14(save_ip_sub_2_7_out_23), .in_15(save_ip_sub_2_7_out_24),
    .in_16(save_ip_sub_2_7_out_25), .in_17(save_ip_sub_2_7_out_26), .in_18(save_ip_sub_2_7_out_27),
    .in_1(out_72), .in_2(out_74), .in_3(out_76), .in_4(out_77), .in_5(out_78), .in_6(out_79), .in_7(out_80),
    .in_8(out_82), .in_9(out_84), .out_19(save_ip_sub_2_8_out_19), .out_20(save_ip_sub_2_8_out_20),
    .out_21(save_ip_sub_2_8_out_21), .out_22(save_ip_sub_2_8_out_22), .out_23(save_ip_sub_2_8_out_23),
    .out_24(save_ip_sub_2_8_out_24), .out_25(save_ip_sub_2_8_out_25), .out_26(save_ip_sub_2_8_out_26),
    .out_27(save_ip_sub_2_8_out_27));
  save_ip_sub_1 save_ip_sub_1_9 (
    .in_1(save_ip_sub_1_8_out_21), .in_2(save_ip_sub_2_8_out_19), .in_3(save_ip_sub_2_8_out_20),
    .in_4(save_ip_sub_2_8_out_21), .in_5(save_ip_sub_2_8_out_22), .in_6(save_ip_sub_2_8_out_23),
    .in_7(save_ip_sub_2_8_out_24), .in_8(save_ip_sub_2_8_out_25), .in_9(save_ip_sub_2_8_out_26),
    .in_10(save_ip_sub_2_8_out_27), .CLEAR(CLEAR), .out_12(out_81), .out_13(out_83), .out_14(out_85),
    .out_15(out_86), .out_16(out_87), .out_17(out_88), .out_18(out_89), .out_19(out_90), .out_20(out_91));  // open: out_21
endmodule

module save_ip_sub_1 (
  input  in_1,
  input  in_2,
  input  in_3,
  input  in_4,
  input  in_5,
  input  in_6,
  input  in_7,
  input  in_8,
  input  in_9,
  input  in_10,
  input  CLEAR,
  output out_12,
  output out_13,
  output out_14,
  output out_15,
  output out_16,
  output out_17,
  output out_18,
  output out_19,
  output out_20,
  output out_21
);

  wire and_1_out, and_2_out, clock_1_out, d_ff_1_qn, d_ff_2_qn, d_ff_3_qn, d_ff_4_qn, d_ff_5_qn, d_ff_6_qn,
       d_ff_7_qn, d_ff_8_qn, d_ff_9_qn;

  Clock clock_1 (.out(clock_1_out));
  and and_1 (and_1_out, in_1, and_2_out);
  D_Flip_Flop d_ff_1 (
    .clk(clock_1_out), .D(in_2), .Q(out_12), .Qn(d_ff_1_qn), .en(and_1_out), .reset(CLEAR));  // open: preset
  D_Flip_Flop d_ff_2 (
    .clk(clock_1_out), .D(in_3), .Q(out_13), .Qn(d_ff_2_qn), .en(and_1_out), .reset(CLEAR));  // open: preset
  D_Flip_Flop d_ff_3 (
    .clk(clock_1_out), .D(in_4), .Q(out_14), .Qn(d_ff_3_qn), .en(and_1_out), .reset(CLEAR));  // open: preset
  D_Flip_Flop d_ff_4 (
    .clk(clock_1_out), .D(in_5), .Q(out_15), .Qn(d_ff_4_qn), .en(and_1_out), .reset(CLEAR));  // open: preset
  D_Flip_Flop d_ff_5 (
    .clk(clock_1_out), .D(in_6), .Q(out_16), .Qn(d_ff_5_qn), .en(and_1_out), .reset(CLEAR));  // open: preset
  D_Flip_Flop d_ff_6 (
    .clk(clock_1_out), .D(in_7), .Q(out_17), .Qn(d_ff_6_qn), .en(and_1_out), .reset(CLEAR));  // open: preset
  D_Flip_Flop d_ff_7 (
    .clk(clock_1_out), .D(in_8), .Q(out_18), .Qn(d_ff_7_qn), .en(and_1_out), .reset(CLEAR));  // open: preset
  D_Flip_Flop d_ff_8 (
    .clk(clock_1_out), .D(in_9), .Q(out_19), .Qn(d_ff_8_qn), .en(and_1_out), .reset(CLEAR));  // open: preset
  D_Flip_Flop d_ff_9 (
    .clk(clock_1_out), .D(in_10), .Q(out_20), .Qn(d_ff_9_qn), .en(and_1_out), .reset(CLEAR));  // open: preset
  or or_1 (out_21, out_12, out_13, out_14, out_15, out_16, out_17, out_18, out_19, out_20);
  and and_2 (and_2_out, d_ff_1_qn, d_ff_2_qn, d_ff_3_qn, d_ff_4_qn, d_ff_5_qn, d_ff_6_qn, d_ff_7_qn, d_ff_8_qn, d_ff_9_qn);
endmodule

module save_ip_sub_2 (
  input  in_1,
  input  in_2,
  input  in_3,
  input  in_4,
  input  in_5,
  input  in_6,
  input  in_7,
  input  in_8,
  input  in_9,
  input  in_10,
  input  in_11,
  input  in_12,
  input  in_13,
  input  in_14,
  input  in_15,
  input  in_16,
  input  in_17,
  input  in_18,
  output out_19,
  output out_20,
  output out_21,
  output out_22,
  output out_23,
  output out_24,
  output out_25,
  output out_26,
  output out_27
);

  wire not_1_out, not_2_out, not_3_out, not_4_out, not_5_out, not_6_out, not_7_out, not_8_out, not_9_out;

  not not_1 (not_1_out, in_1);
  and and_1 (out_19, not_1_out, in_10);
  not not_2 (not_2_out, in_2);
  and and_2 (out_20, not_2_out, in_11);
  not not_3 (not_3_out, in_3);
  and and_3 (out_21, not_3_out, in_12);
  not not_4 (not_4_out, in_4);
  and and_4 (out_22, not_4_out, in_13);
  not not_5 (not_5_out, in_5);
  and and_5 (out_23, not_5_out, in_14);
  not not_6 (not_6_out, in_6);
  and and_6 (out_24, not_6_out, in_15);
  not not_7 (not_7_out, in_7);
  and and_7 (out_25, not_7_out, in_16);
  not not_8 (not_8_out, in_8);
  and and_8 (out_26, not_8_out, in_17);
  not not_9 (not_9_out, in_9);
  and and_9 (out_27, not_9_out, in_18);
endmodule

module connector (
  input  ENABLE,
  input  RESET,
  input  in_3,
  input  in_4,
  input  in_5,
  input  in_6,
  input  in_7,
  input  in_8,
  input  in_9,
  input  in_10,
  input  in_11,
  output [3:0] out_12,
  output [3:0] out_13,
  output [3:0] out_14,
  output [3:0] out_15,
  output [3:0] out_16,
  output [3:0] out_17,
  output [3:0] out_18,
  output [3:0] out_19,
  output [3:0] out_20
);

  wire enable_1_out_11, enable_1_out_12, enable_1_out_13, enable_1_out_14, enable_1_out_15, enable_1_out_16,
       enable_1_out_17, enable_1_out_18, enable_1_out_19, save_inputs_1_out_11, save_inputs_1_out_12,
       save_inputs_1_out_13, save_inputs_1_out_14, save_inputs_1_out_15, save_inputs_1_out_16,
       save_inputs_1_out_17, save_inputs_1_out_18, save_inputs_1_out_19, save_inputs_1_out_20,
       save_inputs_1_out_21, save_inputs_1_out_22, save_inputs_1_out_23, save_inputs_1_out_24,
       save_inputs_1_out_25, save_inputs_1_out_26, save_inputs_1_out_27, save_inputs_1_out_28,
       save_inputs_1_out_29, save_inputs_1_out_30, save_inputs_1_out_31, save_inputs_1_out_32,
       save_inputs_1_out_33, save_inputs_1_out_34, save_inputs_1_out_35, save_inputs_1_out_36,
       save_inputs_1_out_37, save_inputs_1_out_38, save_inputs_1_out_39, save_inputs_1_out_40,
       save_inputs_1_out_41, save_inputs_1_out_42, save_inputs_1_out_43, save_inputs_1_out_44,
       save_inputs_1_out_45, save_inputs_1_out_46, save_inputs_1_out_47, save_inputs_1_out_48,
       save_inputs_1_out_49, save_inputs_1_out_50, save_inputs_1_out_51, save_inputs_1_out_52,
       save_inputs_1_out_53, save_inputs_1_out_54, save_inputs_1_out_55, save_inputs_1_out_56,
       save_inputs_1_out_57, save_inputs_1_out_58, save_inputs_1_out_59, save_inputs_1_out_60,
       save_inputs_1_out_61, save_inputs_1_out_62, save_inputs_1_out_63, save_inputs_1_out_64,
       save_inputs_1_out_65, save_inputs_1_out_66, save_inputs_1_out_67, save_inputs_1_out_68,
       save_inputs_1_out_69, save_inputs_1_out_70, save_inputs_1_out_71, save_inputs_1_out_72,
       save_inputs_1_out_73, save_inputs_1_out_74, save_inputs_1_out_75, save_inputs_1_out_76,
       save_inputs_1_out_77, save_inputs_1_out_78, save_inputs_1_out_79, save_inputs_1_out_80,
       save_inputs_1_out_81, save_inputs_1_out_82, save_inputs_1_out_83, save_inputs_1_out_84,
       save_inputs_1_out_85, save_inputs_1_out_86, save_inputs_1_out_87, save_inputs_1_out_88,
       save_inputs_1_out_89, save_inputs_1_out_90, save_inputs_1_out_91;

  enable enable_1 (
    .in_2(in_3), .in_3(in_4), .in_4(in_5), .in_5(in_6), .in_6(in_7), .in_7(in_8), .in_8(in_9), .in_9(in_10),
    .in_10(in_11), .in_1(ENABLE), .out_11(enable_1_out_11), .out_12(enable_1_out_12),
    .out_13(enable_1_out_13), .out_14(enable_1_out_14), .out_15(enable_1_out_15), .out_16(enable_1_out_16),
    .out_17(enable_1_out_17), .out_18(enable_1_out_18), .out_19(enable_1_out_19));
  Save_Inputs save_inputs_1 (
    .in_1(enable_1_out_11), .in_2(enable_1_out_12), .in_3(enable_1_out_13), .in_4(enable_1_out_14),
    .in_5(enable_1_out_15), .in_6(enable_1_out_16), .in_7(enable_1_out_17), .in_8(enable_1_out_18),
    .in_9(enable_1_out_19), .out_11(save_inputs_1_out_11), .out_12(save_inputs_1_out_12),
    .out_13(save_inputs_1_out_13), .out_14(save_inputs_1_out_14), .out_15(save_inputs_1_out_15),
    .out_16(save_inputs_1_out_16), .out_17(save_inputs_1_out_17), .out_18(save_inputs_1_out_18),
    .out_19(save_inputs_1_out_19), .out_20(save_inputs_1_out_20), .out_21(save_inputs_1_out_21),
    .out_22(save_inputs_1_out_22), .out_23(save_inputs_1_out_23), .out_24(save_inputs_1_out_24),
    .out_25(save_inputs_1_out_25), .out_26(save_inputs_1_out_26), .out_27(save_inputs_1_out_27),
    .out_28(save_inputs_1_out_28), .out_29(save_inputs_1_out_29), .out_30(save_inputs_1_out_30),
    .out_31(save_inputs_1_out_31), .out_32(save_inputs_1_out_32), .out_33(save_inputs_1_out_33),
    .out_34(save_inputs_1_out_34), .out_35(save_inputs_1_out_35), .out_36(save_inputs_1_out_36),
    .out_37(save_inputs_1_out_37), .out_38(save_inputs_1_out_38), .out_39(save_inputs_1_out_39),
    .out_40(save_inputs_1_out_40), .out_41(save_inputs_1_out_41), .out_42(save_inputs_1_out_42),
    .out_43(save_inputs_1_out_43), .out_44(save_inputs_1_out_44), .out_45(save_inputs_1_out_45),
    .out_46(save_inputs_1_out_46), .out_47(save_inputs_1_out_47), .out_48(save_inputs_1_out_48),
    .out_49(save_inputs_1_out_49), .out_50(save_inputs_1_out_50), .out_51(save_inputs_1_out_51),
    .out_52(save_inputs_1_out_52), .out_53(save_inputs_1_out_53), .out_54(save_inputs_1_out_54),
    .out_55(save_inputs_1_out_55), .out_56(save_inputs_1_out_56), .out_57(save_inputs_1_out_57),
    .out_58(save_inputs_1_out_58), .out_59(save_inputs_1_out_59), .out_60(save_inputs_1_out_60),
    .out_61(save_inputs_1_out_61), .out_62(save_inputs_1_out_62), .out_63(save_inputs_1_out_63),
    .out_64(save_inputs_1_out_64), .out_65(save_inputs_1_out_65), .out_66(save_inputs_1_out_66),
    .out_67(save_inputs_1_out_67), .out_68(save_inputs_1_out_68), .out_69(save_inputs_1_out_69),
    .out_70(save_inputs_1_out_70), .out_71(save_inputs_1_out_71), .out_72(save_inputs_1_out_72),
    .out_73(save_inputs_1_out_73), .out_74(save_inputs_1_out_74), .out_75(save_inputs_1_out_75),
    .out_76(save_inputs_1_out_76), .out_77(save_inputs_1_out_77), .out_78(save_inputs_1_out_78),
    .out_79(save_inputs_1_out_79), .out_80(save_inputs_1_out_80), .out_81(save_inputs_1_out_81),
    .out_82(save_inputs_1_out_82), .out_83(save_inputs_1_out_83), .out_84(save_inputs_1_out_84),
    .out_85(save_inputs_1_out_85), .out_86(save_inputs_1_out_86), .out_87(save_inputs_1_out_87),
    .out_88(save_inputs_1_out_88), .out_89(save_inputs_1_out_89), .out_90(save_inputs_1_out_90),
    .out_91(save_inputs_1_out_91), .CLEAR(RESET));
  Priority_Encoder #(.select(4)) priority_encoder_1 (
    .in0(1'b1), .in1(save_inputs_1_out_11), .in2(save_inputs_1_out_12), .in3(save_inputs_1_out_13),
    .in4(save_inputs_1_out_14), .in5(save_inputs_1_out_15), .in6(save_inputs_1_out_16),
    .in7(save_inputs_1_out_17), .in8(save_inputs_1_out_19), .in9(save_inputs_1_out_21), .out(out_12));  // open: in10, in11, in12, in13, in14, in15, gs, en_out, en_in
  Priority_Encoder #(.select(4)) priority_encoder_2 (
    .in0(1'b1), .in1(save_inputs_1_out_18), .in2(save_inputs_1_out_20), .in3(save_inputs_1_out_22),
    .in4(save_inputs_1_out_23), .in5(save_inputs_1_out_24), .in6(save_inputs_1_out_25),
    .in7(save_inputs_1_out_26), .in8(save_inputs_1_out_28), .in9(save_inputs_1_out_30), .out(out_13));  // open: in10, in11, in12, in13, in14, in15, gs, en_out, en_in
  Priority_Encoder #(.select(4)) priority_encoder_3 (
    .in0(1'b1), .in1(save_inputs_1_out_27), .in2(save_inputs_1_out_29), .in3(save_inputs_1_out_31),
    .in4(save_inputs_1_out_32), .in5(save_inputs_1_out_33), .in6(save_inputs_1_out_34),
    .in7(save_inputs_1_out_35), .in8(save_inputs_1_out_37), .in9(save_inputs_1_out_39), .out(out_14));  // open: in10, in11, in12, in13, in14, in15, gs, en_out, en_in
  Priority_Encoder #(.select(4)) priority_encoder_4 (
    .in0(1'b1), .in1(save_inputs_1_out_36), .in2(save_inputs_1_out_38), .in3(save_inputs_1_out_40),
    .in4(save_inputs_1_out_41), .in5(save_inputs_1_out_42), .in6(save_inputs_1_out_43),
    .in7(save_inputs_1_out_44), .in8(save_inputs_1_out_46), .in9(save_inputs_1_out_48), .out(out_15));  // open: in10, in11, in12, in13, in14, in15, gs, en_out, en_in
  Priority_Encoder #(.select(4)) priority_encoder_5 (
    .in0(1'b1), .in1(save_inputs_1_out_45), .in2(save_inputs_1_out_47), .in3(save_inputs_1_out_49),
    .in4(save_inputs_1_out_50), .in5(save_inputs_1_out_51), .in6(save_inputs_1_out_52),
    .in7(save_inputs_1_out_53), .in8(save_inputs_1_out_55), .in9(save_inputs_1_out_57), .out(out_16));  // open: in10, in11, in12, in13, in14, in15, gs, en_out, en_in
  Priority_Encoder #(.select(4)) priority_encoder_6 (
    .in0(1'b1), .in1(save_inputs_1_out_54), .in2(save_inputs_1_out_56), .in3(save_inputs_1_out_58),
    .in4(save_inputs_1_out_59), .in5(save_inputs_1_out_60), .in6(save_inputs_1_out_61),
    .in7(save_inputs_1_out_62), .in8(save_inputs_1_out_64), .in9(save_inputs_1_out_66), .out(out_17));  // open: in10, in11, in12, in13, in14, in15, gs, en_out, en_in
  Priority_Encoder #(.select(4)) priority_encoder_7 (
    .in0(1'b1), .in1(save_inputs_1_out_63), .in2(save_inputs_1_out_65), .in3(save_inputs_1_out_67),
    .in4(save_inputs_1_out_68), .in5(save_inputs_1_out_69), .in6(save_inputs_1_out_70),
    .in7(save_inputs_1_out_71), .in8(save_inputs_1_out_73), .in9(save_inputs_1_out_75), .out(out_18));  // open: in10, in11, in12, in13, in14, in15, gs, en_out, en_in
  Priority_Encoder #(.select(4)) priority_encoder_8 (
    .in0(1'b1), .in1(save_inputs_1_out_72), .in2(save_inputs_1_out_74), .in3(save_inputs_1_out_76),
    .in4(save_inputs_1_out_77), .in5(save_inputs_1_out_78), .in6(save_inputs_1_out_79),
    .in7(save_inputs_1_out_80), .in8(save_inputs_1_out_82), .in9(save_inputs_1_out_84), .out(out_19));  // open: in10, in11, in12, in13, in14, in15, gs, en_out, en_in
  Priority_Encoder #(.select(4)) priority_encoder_9 (
    .in0(1'b1), .in1(save_inputs_1_out_81), .in2(save_inputs_1_out_83), .in3(save_inputs_1_out_85),
    .in4(save_inputs_1_out_86), .in5(save_inputs_1_out_87), .in6(save_inputs_1_out_88),
    .in7(save_inputs_1_out_89), .in8(save_inputs_1_out_90), .in9(save_inputs_1_out_91), .out(out_20));  // open: in10, in11, in12, in13, in14, in15, gs, en_out, en_in
endmodule

module display_encode_sub1 (
  input  in_1,
  input  in_2,
  input  in_3,
  input  in_4,
  input  in_5,
  input  in_6,
  input  in_7,
  input  in_8,
  input  in_9,
  output out_10,
  output out_11,
  output out_12,
  output out_13,
  output out_14,
  output out_15,
  output out_16,
  output out_17,
  output out_18
);

  wire decoder_1_out1, decoder_1_out2, decoder_1_out3, decoder_1_out4, decoder_1_out5, decoder_1_out6,
       decoder_1_out7, decoder_1_out8, decoder_1_out9, decoder_2_out1, decoder_2_out2, decoder_2_out3,
       decoder_2_out4, decoder_2_out5, decoder_2_out6, decoder_2_out7, decoder_2_out8, decoder_2_out9,
       decoder_3_out1, decoder_3_out2, decoder_3_out3, decoder_3_out4, decoder_3_out5, decoder_3_out6,
       decoder_3_out7, decoder_3_out8, decoder_3_out9, save_ip_sub_2_1_out_19, save_ip_sub_2_1_out_20,
       save_ip_sub_2_1_out_21, save_ip_sub_2_1_out_22, save_ip_sub_2_1_out_23, save_ip_sub_2_1_out_24,
       save_ip_sub_2_1_out_25, save_ip_sub_2_1_out_26, save_ip_sub_2_1_out_27;
  wire [3:0] priority_encoder_1_out, priority_encoder_2_out;

  Priority_Encoder #(.select(4)) priority_encoder_1 (
    .in0(1'b1), .in1(in_1), .in2(in_2), .in3(in_3), .in4(in_4), .in5(in_5), .in6(in_6), .in7(in_7),
    .in8(in_8), .in9(in_9), .out(priority_encoder_1_out));  // open: in10, in11, in12, in13, in14, in15, gs, en_out, en_in
  Decoder #(.select(4), .disabled(0)) decoder_1 (
    .out1(decoder_1_out1), .out2(decoder_1_out2), .out3(decoder_1_out3), .out4(decoder_1_out4),
    .out5(decoder_1_out5), .out6(decoder_1_out6), .out7(decoder_1_out7), .out8(decoder_1_out8),
    .out9(decoder_1_out9), .sel(priority_encoder_1_out));  // open: out0, out10, out11, out12, out13, out14, out15, en
  save_ip_sub_2 save_ip_sub_2_1 (
    .in_10(in_1), .in_11(in_2), .in_12(in_3), .in_13(in_4), .in_14(in_5), .in_15(in_6), .in_16(in_7),
    .in_17(in_8), .in_18(in_9), .in_1(decoder_1_out1), .in_2(decoder_1_out2), .in_3(decoder_1_out3),
    .in_4(decoder_1_out4), .in_5(decoder_1_out5), .in_6(decoder_1_out6), .in_7(decoder_1_out7),
    .in_8(decoder_1_out8), .in_9(decoder_1_out9), .out_19(save_ip_sub_2_1_out_19),
    .out_20(save_ip_sub_2_1_out_20), .out_21(save_ip_sub_2_1_out_21), .out_22(save_ip_sub_2_1_out_22),
    .out_23(save_ip_sub_2_1_out_23), .out_24(save_ip_sub_2_1_out_24), .out_25(save_ip_sub_2_1_out_25),
    .out_26(save_ip_sub_2_1_out_26), .out_27(save_ip_sub_2_1_out_27));
  Priority_Encoder #(.select(4)) priority_encoder_2 (
    .in0(1'b1), .in1(save_ip_sub_2_1_out_19), .in2(save_ip_sub_2_1_out_20), .in3(save_ip_sub_2_1_out_21),
    .in4(save_ip_sub_2_1_out_22), .in5(save_ip_sub_2_1_out_23), .in6(save_ip_sub_2_1_out_24),
    .in7(save_ip_sub_2_1_out_25), .in8(save_ip_sub_2_1_out_26), .in9(save_ip_sub_2_1_out_27),
    .out(priority_encoder_2_out));  // open: in10, in11, in12, in13, in14, in15, gs, en_out, en_in
  Decoder #(.select(4)) decoder_2 (
    .out1(decoder_2_out1), .out2(decoder_2_out2), .out3(decoder_2_out3), .out4(decoder_2_out4),
    .out5(decoder_2_out5), .out6(decoder_2_out6), .out7(decoder_2_out7), .out8(decoder_2_out8),
    .out9(decoder_2_out9), .sel(priority_encoder_1_out));  // open: out0, out10, out11, out12, out13, out14, out15, en
  Decoder #(.select(4)) decoder_3 (
    .out1(decoder_3_out1), .out2(decoder_3_out2), .out3(decoder_3_out3), .out4(decoder_3_out4),
    .out5(decoder_3_out5), .out6(decoder_3_out6), .out7(decoder_3_out7), .out8(decoder_3_out8),
    .out9(decoder_3_out9), .sel(priority_encoder_2_out));  // open: out0, out10, out11, out12, out13, out14, out15, en
  or or_1 (out_10, decoder_2_out1, decoder_3_out1);
  or or_2 (out_11, decoder_2_out2, decoder_3_out2);
  or or_3 (out_12, decoder_2_out3, decoder_3_out3);
  or or_4 (out_13, decoder_2_out4, decoder_3_out4);
  or or_5 (out_14, decoder_2_out5, decoder_3_out5);
  or or_6 (out_15, decoder_2_out6, decoder_3_out6);
  or or_7 (out_16, decoder_2_out7, decoder_3_out7);
  or or_8 (out_17, decoder_2_out8, decoder_3_out8);
  or or_9 (out_18, decoder_2_out9, decoder_3_out9);
endmodule

module display_encode_sub_2 (
  input  in_1,
  input  in_2,
  input  in_3,
  input  in_4,
  input  in_5,
  input  in_6,
  input  in_7,
  input  in_8,
  input  in_9,
  input  in_10,
  output out_11,
  output out_12,
  output out_13,
  output out_14,
  output out_15,
  output out_16,
  output out_17,
  output out_18,
  output out_19
);

  and and_1 (out_11, in_1, in_10);
  and and_2 (out_12, in_2, in_10);
  and and_3 (out_13, in_3, in_10);
  and and_4 (out_14, in_4, in_10);
  and and_5 (out_15, in_5, in_10);
  and and_6 (out_16, in_6, in_10);
  and and_7 (out_17, in_7, in_10);
  and and_8 (out_18, in_8, in_10);
  and and_9 (out_19, in_9, in_10);
endmodule

module display_encode (
  input  in_1,
  input  in_2,
  input  in_3,
  input  in_4,
  input  in_5,
  input  in_6,
  input  in_7,
  input  in_8,
  input  in_9,
  input  CLEAR,
  output out_11,
  output out_12,
  output out_13,
  output out_14,
  output out_15,
  output out_16,
  output out_17,
  output out_18,
  output out_19
);

  wire display_encode_sub1_1_out_10, display_encode_sub1_1_out_11, display_encode_sub1_1_out_12,
       display_encode_sub1_1_out_13, display_encode_sub1_1_out_14, display_encode_sub1_1_out_15,
       display_encode_sub1_1_out_16, display_encode_sub1_1_out_17, display_encode_sub1_1_out_18,
       display_encode_sub_2_1_out_11, display_encode_sub_2_1_out_12, display_encode_sub_2_1_out_13,
       display_encode_sub_2_1_out_14, display_encode_sub_2_1_out_15, display_encode_sub_2_1_out_16,
       display_encode_sub_2_1_out_17, display_encode_sub_2_1_out_18, display_encode_sub_2_1_out_19,
       display_encode_sub_2_2_out_11, display_encode_sub_2_2_out_12, display_encode_sub_2_2_out_13,
       display_encode_sub_2_2_out_14, display_encode_sub_2_2_out_15, display_encode_sub_2_2_out_16,
       display_encode_sub_2_2_out_17, display_encode_sub_2_2_out_18, display_encode_sub_2_2_out_19,
       display_encode_sub_2_3_out_11, display_encode_sub_2_3_out_12, display_encode_sub_2_3_out_13,
       display_encode_sub_2_3_out_14, display_encode_sub_2_3_out_15, display_encode_sub_2_3_out_16,
       display_encode_sub_2_3_out_17, display_encode_sub_2_3_out_18, display_encode_sub_2_3_out_19,
       display_encode_sub_2_4_out_11, display_encode_sub_2_4_out_12, display_encode_sub_2_4_out_13,
       display_encode_sub_2_4_out_14, display_encode_sub_2_4_out_15, display_encode_sub_2_4_out_16,
       display_encode_sub_2_4_out_17, display_encode_sub_2_4_out_18, display_encode_sub_2_4_out_19,
       display_encode_sub_2_5_out_11, display_encode_sub_2_5_out_12, display_encode_sub_2_5_out_13,
       display_encode_sub_2_5_out_14, display_encode_sub_2_5_out_15, display_encode_sub_2_5_out_16,
       display_encode_sub_2_5_out_17, display_encode_sub_2_5_out_18, display_encode_sub_2_5_out_19,
       display_encode_sub_2_6_out_11, display_encode_sub_2_6_out_12, display_encode_sub_2_6_out_13,
       display_encode_sub_2_6_out_14, display_encode_sub_2_6_out_15, display_encode_sub_2_6_out_16,
       display_encode_sub_2_6_out_17, display_encode_sub_2_6_out_18, display_encode_sub_2_6_out_19,
       display_encode_sub_2_7_out_11, display_encode_sub_2_7_out_12, display_encode_sub_2_7_out_13,
       display_encode_sub_2_7_out_14, display_encode_sub_2_7_out_15, display_encode_sub_2_7_out_16,
       display_encode_sub_2_7_out_17, display_encode_sub_2_7_out_18, display_encode_sub_2_7_out_19,
       display_encode_sub_2_8_out_11, display_encode_sub_2_8_out_12, display_encode_sub_2_8_out_13,
       display_encode_sub_2_8_out_14, display_encode_sub_2_8_out_15, display_encode_sub_2_8_out_16,
       display_encode_sub_2_8_out_17, display_encode_sub_2_8_out_18, display_encode_sub_2_8_out_19,
       display_encode_sub_2_9_out_11, display_encode_sub_2_9_out_12, display_encode_sub_2_9_out_13,
       display_encode_sub_2_9_out_14, display_encode_sub_2_9_out_15, display_encode_sub_2_9_out_16,
       display_encode_sub_2_9_out_17, display_encode_sub_2_9_out_18, display_encode_sub_2_9_out_19,
       or_10_out, or_11_out, or_12_out, or_13_out, or_14_out, or_15_out, or_16_out, or_17_out, or_18_out,
       save_inputs_1_out_11, save_inputs_1_out_12, save_inputs_1_out_13, save_inputs_1_out_14,
       save_inputs_1_out_15, save_inputs_1_out_16, save_inputs_1_out_17, save_inputs_1_out_18,
       save_inputs_1_out_19, save_inputs_1_out_20, save_inputs_1_out_21, save_inputs_1_out_22,
       save_inputs_1_out_23, save_inputs_1_out_24, save_inputs_1_out_25, save_inputs_1_out_26,
       save_inputs_1_out_27, save_inputs_1_out_28, save_inputs_1_out_29, save_inputs_1_out_30,
       save_inputs_1_out_31, save_inputs_1_out_32, save_inputs_1_out_33, save_inputs_1_out_34,
       save_inputs_1_out_35, save_inputs_1_out_36, save_inputs_1_out_37, save_inputs_1_out_38,
       save_inputs_1_out_39, save_inputs_1_out_40, save_inputs_1_out_41, save_inputs_1_out_42,
       save_inputs_1_out_43, save_inputs_1_out_44, save_inputs_1_out_45, save_inputs_1_out_46,
       save_inputs_1_out_47, save_inputs_1_out_48, save_inputs_1_out_49, save_inputs_1_out_50,
       save_inputs_1_out_51, save_inputs_1_out_52, save_inputs_1_out_53, save_inputs_1_out_54,
       save_inputs_1_out_55, save_inputs_1_out_56, save_inputs_1_out_57, save_inputs_1_out_58,
       save_inputs_1_out_59, save_inputs_1_out_60, save_inputs_1_out_61, save_inputs_1_out_62,
       save_inputs_1_out_63, save_inputs_1_out_64, save_inputs_1_out_65, save_inputs_1_out_66,
       save_inputs_1_out_67, save_inputs_1_out_68, save_inputs_1_out_69, save_inputs_1_out_70,
       save_inputs_1_out_71, save_inputs_1_out_72, save_inputs_1_out_73, save_inputs_1_out_74,
       save_inputs_1_out_75, save_inputs_1_out_76, save_inputs_1_out_77, save_inputs_1_out_78,
       save_inputs_1_out_79, save_inputs_1_out_80, save_inputs_1_out_81, save_inputs_1_out_82,
       save_inputs_1_out_83, save_inputs_1_out_84, save_inputs_1_out_85, save_inputs_1_out_86,
       save_inputs_1_out_87, save_inputs_1_out_88, save_inputs_1_out_89, save_inputs_1_out_90,
       save_inputs_1_out_91;

  Save_Inputs save_inputs_1 (
    .in_1(in_1), .in_2(in_2), .in_3(in_3), .in_4(in_4), .in_5(in_5), .in_6(in_6), .in_7(in_7), .in_8(in_8),
    .in_9(in_9), .out_11(save_inputs_1_out_11), .out_12(save_inputs_1_out_12), .out_13(save_inputs_1_out_13),
    .out_14(save_inputs_1_out_14), .out_15(save_inputs_1_out_15), .out_16(save_inputs_1_out_16),
    .out_17(save_inputs_1_out_17), .out_18(save_inputs_1_out_18), .out_19(save_inputs_1_out_19),
    .out_20(save_inputs_1_out_20), .out_21(save_inputs_1_out_21), .out_22(save_inputs_1_out_22),
    .out_23(save_inputs_1_out_23), .out_24(save_inputs_1_out_24), .out_25(save_inputs_1_out_25),
    .out_26(save_inputs_1_out_26), .out_27(save_inputs_1_out_27), .out_28(save_inputs_1_out_28),
    .out_29(save_inputs_1_out_29), .out_30(save_inputs_1_out_30), .out_31(save_inputs_1_out_31),
    .out_32(save_inputs_1_out_32), .out_33(save_inputs_1_out_33), .out_34(save_inputs_1_out_34),
    .out_35(save_inputs_1_out_35), .out_36(save_inputs_1_out_36), .out_37(save_inputs_1_out_37),
    .out_38(save_inputs_1_out_38), .out_39(save_inputs_1_out_39), .out_40(save_inputs_1_out_40),
    .out_41(save_inputs_1_out_41), .out_42(save_inputs_1_out_42), .out_43(save_inputs_1_out_43),
    .out_44(save_inputs_1_out_44), .out_45(save_inputs_1_out_45), .out_46(save_inputs_1_out_46),
    .out_47(save_inputs_1_out_47), .out_48(save_inputs_1_out_48), .out_49(save_inputs_1_out_49),
    .out_50(save_inputs_1_out_50), .out_51(save_inputs_1_out_51), .out_52(save_inputs_1_out_52),
    .out_53(save_inputs_1_out_53), .out_54(save_inputs_1_out_54), .out_55(save_inputs_1_out_55),
    .out_56(save_inputs_1_out_56), .out_57(save_inputs_1_out_57), .out_58(save_inputs_1_out_58),
    .out_59(save_inputs_1_out_59), .out_60(save_inputs_1_out_60), .out_61(save_inputs_1_out_61),
    .out_62(save_inputs_1_out_62), .out_63(save_inputs_1_out_63), .out_64(save_inputs_1_out_64),
    .out_65(save_inputs_1_out_65), .out_66(save_inputs_1_out_66), .out_67(save_inputs_1_out_67),
    .out_68(save_inputs_1_out_68), .out_69(save_inputs_1_out_69), .out_70(save_inputs_1_out_70),
    .out_71(save_inputs_1_out_71), .out_72(save_inputs_1_out_72), .out_73(save_inputs_1_out_73),
    .out_74(save_inputs_1_out_74), .out_75(save_inputs_1_out_75), .out_76(save_inputs_1_out_76),
    .out_77(save_inputs_1_out_77), .out_78(save_inputs_1_out_78), .out_79(save_inputs_1_out_79),
    .out_80(save_inputs_1_out_80), .out_81(save_inputs_1_out_81), .out_82(save_inputs_1_out_82),
    .out_83(save_inputs_1_out_83), .out_84(save_inputs_1_out_84), .out_85(save_inputs_1_out_85),
    .out_86(save_inputs_1_out_86), .out_87(save_inputs_1_out_87), .out_88(save_inputs_1_out_88),
    .out_89(save_inputs_1_out_89), .out_90(save_inputs_1_out_90), .out_91(save_inputs_1_out_91), .CLEAR(CLEAR));
  display_encode_sub_2 display_encode_sub_2_1 (
    .in_1(save_inputs_1_out_11), .in_2(save_inputs_1_out_12), .in_3(save_inputs_1_out_13),
    .in_4(save_inputs_1_out_14), .in_5(save_inputs_1_out_15), .in_6(save_inputs_1_out_16),
    .in_7(save_inputs_1_out_17), .in_8(save_inputs_1_out_19), .in_9(save_inputs_1_out_21),
    .out_11(display_encode_sub_2_1_out_11), .out_12(display_encode_sub_2_1_out_12),
    .out_13(display_encode_sub_2_1_out_13), .out_14(display_encode_sub_2_1_out_14),
    .out_15(display_encode_sub_2_1_out_15), .out_16(display_encode_sub_2_1_out_16),
    .out_17(display_encode_sub_2_1_out_17), .out_18(display_encode_sub_2_1_out_18),
    .out_19(display_encode_sub_2_1_out_19), .in_10(display_encode_sub1_1_out_10));
  display_encode_sub_2 display_encode_sub_2_2 (
    .in_1(save_inputs_1_out_18), .in_2(save_inputs_1_out_20), .in_3(save_inputs_1_out_22),
    .in_4(save_inputs_1_out_23), .in_5(save_inputs_1_out_24), .in_6(save_inputs_1_out_25),
    .in_7(save_inputs_1_out_26), .in_8(save_inputs_1_out_28), .in_9(save_inputs_1_out_30),
    .out_11(display_encode_sub_2_2_out_11), .out_12(display_encode_sub_2_2_out_12),
    .out_13(display_encode_sub_2_2_out_13), .out_14(display_encode_sub_2_2_out_14),
    .out_15(display_encode_sub_2_2_out_15), .out_16(display_encode_sub_2_2_out_16),
    .out_17(display_encode_sub_2_2_out_17), .out_18(display_encode_sub_2_2_out_18),
    .out_19(display_encode_sub_2_2_out_19), .in_10(display_encode_sub1_1_out_11));
  display_encode_sub_2 display_encode_sub_2_3 (
    .in_1(save_inputs_1_out_27), .in_2(save_inputs_1_out_29), .in_3(save_inputs_1_out_31),
    .in_4(save_inputs_1_out_32), .in_5(save_inputs_1_out_33), .in_6(save_inputs_1_out_34),
    .in_7(save_inputs_1_out_35), .in_8(save_inputs_1_out_37), .in_9(save_inputs_1_out_39),
    .out_11(display_encode_sub_2_3_out_11), .out_12(display_encode_sub_2_3_out_12),
    .out_13(display_encode_sub_2_3_out_13), .out_14(display_encode_sub_2_3_out_14),
    .out_15(display_encode_sub_2_3_out_15), .out_16(display_encode_sub_2_3_out_16),
    .out_17(display_encode_sub_2_3_out_17), .out_18(display_encode_sub_2_3_out_18),
    .out_19(display_encode_sub_2_3_out_19), .in_10(display_encode_sub1_1_out_12));
  display_encode_sub_2 display_encode_sub_2_4 (
    .in_1(save_inputs_1_out_36), .in_2(save_inputs_1_out_38), .in_3(save_inputs_1_out_40),
    .in_4(save_inputs_1_out_41), .in_5(save_inputs_1_out_42), .in_6(save_inputs_1_out_43),
    .in_7(save_inputs_1_out_44), .in_8(save_inputs_1_out_46), .in_9(save_inputs_1_out_48),
    .out_11(display_encode_sub_2_4_out_11), .out_12(display_encode_sub_2_4_out_12),
    .out_13(display_encode_sub_2_4_out_13), .out_14(display_encode_sub_2_4_out_14),
    .out_15(display_encode_sub_2_4_out_15), .out_16(display_encode_sub_2_4_out_16),
    .out_17(display_encode_sub_2_4_out_17), .out_18(display_encode_sub_2_4_out_18),
    .out_19(display_encode_sub_2_4_out_19), .in_10(display_encode_sub1_1_out_13));
  display_encode_sub_2 display_encode_sub_2_5 (
    .in_1(save_inputs_1_out_45), .in_2(save_inputs_1_out_47), .in_3(save_inputs_1_out_49),
    .in_4(save_inputs_1_out_50), .in_5(save_inputs_1_out_51), .in_6(save_inputs_1_out_52),
    .in_7(save_inputs_1_out_53), .in_8(save_inputs_1_out_55), .in_9(save_inputs_1_out_57),
    .out_11(display_encode_sub_2_5_out_11), .out_12(display_encode_sub_2_5_out_12),
    .out_13(display_encode_sub_2_5_out_13), .out_14(display_encode_sub_2_5_out_14),
    .out_15(display_encode_sub_2_5_out_15), .out_16(display_encode_sub_2_5_out_16),
    .out_17(display_encode_sub_2_5_out_17), .out_18(display_encode_sub_2_5_out_18),
    .out_19(display_encode_sub_2_5_out_19), .in_10(display_encode_sub1_1_out_14));
  display_encode_sub_2 display_encode_sub_2_6 (
    .in_1(save_inputs_1_out_54), .in_2(save_inputs_1_out_56), .in_3(save_inputs_1_out_58),
    .in_4(save_inputs_1_out_59), .in_5(save_inputs_1_out_60), .in_6(save_inputs_1_out_61),
    .in_7(save_inputs_1_out_62), .in_8(save_inputs_1_out_64), .in_9(save_inputs_1_out_66),
    .out_11(display_encode_sub_2_6_out_11), .out_12(display_encode_sub_2_6_out_12),
    .out_13(display_encode_sub_2_6_out_13), .out_14(display_encode_sub_2_6_out_14),
    .out_15(display_encode_sub_2_6_out_15), .out_16(display_encode_sub_2_6_out_16),
    .out_17(display_encode_sub_2_6_out_17), .out_18(display_encode_sub_2_6_out_18),
    .out_19(display_encode_sub_2_6_out_19), .in_10(display_encode_sub1_1_out_15));
  display_encode_sub_2 display_encode_sub_2_7 (
    .in_1(save_inputs_1_out_63), .in_2(save_inputs_1_out_65), .in_3(save_inputs_1_out_67),
    .in_4(save_inputs_1_out_68), .in_5(save_inputs_1_out_69), .in_6(save_inputs_1_out_70),
    .in_7(save_inputs_1_out_71), .in_8(save_inputs_1_out_73), .in_9(save_inputs_1_out_75),
    .out_11(display_encode_sub_2_7_out_11), .out_12(display_encode_sub_2_7_out_12),
    .out_13(display_encode_sub_2_7_out_13), .out_14(display_encode_sub_2_7_out_14),
    .out_15(display_encode_sub_2_7_out_15), .out_16(display_encode_sub_2_7_out_16),
    .out_17(display_encode_sub_2_7_out_17), .out_18(display_encode_sub_2_7_out_18),
    .out_19(display_encode_sub_2_7_out_19), .in_10(display_encode_sub1_1_out_16));
  display_encode_sub_2 display_encode_sub_2_8 (
    .in_1(save_inputs_1_out_72), .in_2(save_inputs_1_out_74), .in_3(save_inputs_1_out_76),
    .in_4(save_inputs_1_out_77), .in_5(save_inputs_1_out_78), .in_6(save_inputs_1_out_79),
    .in_7(save_inputs_1_out_80), .in_8(save_inputs_1_out_82), .in_9(save_inputs_1_out_84),
    .out_11(display_encode_sub_2_8_out_11), .out_12(display_encode_sub_2_8_out_12),
    .out_13(display_encode_sub_2_8_out_13), .out_14(display_encode_sub_2_8_out_14),
    .out_15(display_encode_sub_2_8_out_15), .out_16(display_encode_sub_2_8_out_16),
    .out_17(display_encode_sub_2_8_out_17), .out_18(display_encode_sub_2_8_out_18),
    .out_19(display_encode_sub_2_8_out_19), .in_10(display_encode_sub1_1_out_17));
  display_encode_sub_2 display_encode_sub_2_9 (
    .in_1(save_inputs_1_out_81), .in_2(save_inputs_1_out_83), .in_3(save_inputs_1_out_85),
    .in_4(save_inputs_1_out_86), .in_5(save_inputs_1_out_87), .in_6(save_inputs_1_out_88),
    .in_7(save_inputs_1_out_89), .in_8(save_inputs_1_out_90), .in_9(save_inputs_1_out_91),
    .out_11(display_encode_sub_2_9_out_11), .out_12(display_encode_sub_2_9_out_12),
    .out_13(display_encode_sub_2_9_out_13), .out_14(display_encode_sub_2_9_out_14),
    .out_15(display_encode_sub_2_9_out_15), .out_16(display_encode_sub_2_9_out_16),
    .out_17(display_encode_sub_2_9_out_17), .out_18(display_encode_sub_2_9_out_18),
    .out_19(display_encode_sub_2_9_out_19), .in_10(display_encode_sub1_1_out_18));
  or or_1 (out_11, display_encode_sub_2_1_out_11, display_encode_sub_2_2_out_11, display_encode_sub_2_3_out_11, display_encode_sub_2_4_out_11, display_encode_sub_2_5_out_11, display_encode_sub_2_6_out_11, display_encode_sub_2_7_out_11, display_encode_sub_2_8_out_11, display_encode_sub_2_9_out_11);
  or or_2 (out_12, display_encode_sub_2_1_out_12, display_encode_sub_2_2_out_12, display_encode_sub_2_3_out_12, display_encode_sub_2_4_out_12, display_encode_sub_2_5_out_12, display_encode_sub_2_6_out_12, display_encode_sub_2_7_out_12, display_encode_sub_2_8_out_12, display_encode_sub_2_9_out_12);
  or or_3 (out_13, display_encode_sub_2_1_out_13, display_encode_sub_2_2_out_13, display_encode_sub_2_3_out_13, display_encode_sub_2_4_out_13, display_encode_sub_2_5_out_13, display_encode_sub_2_6_out_13, display_encode_sub_2_7_out_13, display_encode_sub_2_8_out_13, display_encode_sub_2_9_out_13);
  or or_4 (out_14, display_encode_sub_2_1_out_14, display_encode_sub_2_2_out_14, display_encode_sub_2_3_out_14, display_encode_sub_2_4_out_14, display_encode_sub_2_5_out_14, display_encode_sub_2_6_out_14, display_encode_sub_2_7_out_14, display_encode_sub_2_8_out_14, display_encode_sub_2_9_out_14);
  or or_5 (out_15, display_encode_sub_2_1_out_15, display_encode_sub_2_2_out_15, display_encode_sub_2_3_out_15, display_encode_sub_2_4_out_15, display_encode_sub_2_5_out_15, display_encode_sub_2_6_out_15, display_encode_sub_2_7_out_15, display_encode_sub_2_8_out_15, display_encode_sub_2_9_out_15);
  or or_6 (out_16, display_encode_sub_2_1_out_16, display_encode_sub_2_2_out_16, display_encode_sub_2_3_out_16, display_encode_sub_2_4_out_16, display_encode_sub_2_5_out_16, display_encode_sub_2_6_out_16, display_encode_sub_2_7_out_16, display_encode_sub_2_8_out_16, display_encode_sub_2_9_out_16);
  or or_7 (out_17, display_encode_sub_2_1_out_17, display_encode_sub_2_2_out_17, display_encode_sub_2_3_out_17, display_encode_sub_2_4_out_17, display_encode_sub_2_5_out_17, display_encode_sub_2_6_out_17, display_encode_sub_2_7_out_17, display_encode_sub_2_8_out_17, display_encode_sub_2_9_out_17);
  or or_8 (out_18, display_encode_sub_2_1_out_18, display_encode_sub_2_2_out_18, display_encode_sub_2_3_out_18, display_encode_sub_2_4_out_18, display_encode_sub_2_5_out_18, display_encode_sub_2_6_out_18, display_encode_sub_2_7_out_18, display_encode_sub_2_8_out_18, display_encode_sub_2_9_out_18);
  or or_9 (out_19, display_encode_sub_2_1_out_19, display_encode_sub_2_2_out_19, display_encode_sub_2_3_out_19, display_encode_sub_2_4_out_19, display_encode_sub_2_5_out_19, display_encode_sub_2_6_out_19, display_encode_sub_2_7_out_19, display_encode_sub_2_8_out_19, display_encode_sub_2_9_out_19);
  or or_10 (or_10_out, save_inputs_1_out_11, save_inputs_1_out_12, save_inputs_1_out_13, save_inputs_1_out_14, save_inputs_1_out_15, save_inputs_1_out_16, save_inputs_1_out_17, save_inputs_1_out_19, save_inputs_1_out_21);
  or or_11 (or_11_out, save_inputs_1_out_18, save_inputs_1_out_20, save_inputs_1_out_22, save_inputs_1_out_23, save_inputs_1_out_24, save_inputs_1_out_25, save_inputs_1_out_26, save_inputs_1_out_28, save_inputs_1_out_30);
  or or_12 (or_12_out, save_inputs_1_out_27, save_inputs_1_out_29, save_inputs_1_out_31, save_inputs_1_out_32, save_inputs_1_out_33, save_inputs_1_out_34, save_inputs_1_out_35, save_inputs_1_out_37, save_inputs_1_out_39);
  or or_13 (or_13_out, save_inputs_1_out_36, save_inputs_1_out_38, save_inputs_1_out_40, save_inputs_1_out_41, save_inputs_1_out_42, save_inputs_1_out_43, save_inputs_1_out_44, save_inputs_1_out_46, save_inputs_1_out_48);
  or or_14 (or_14_out, save_inputs_1_out_45, save_inputs_1_out_47, save_inputs_1_out_49, save_inputs_1_out_50, save_inputs_1_out_51, save_inputs_1_out_52, save_inputs_1_out_53, save_inputs_1_out_55, save_inputs_1_out_57);
  or or_15 (or_15_out, save_inputs_1_out_54, save_inputs_1_out_56, save_inputs_1_out_58, save_inputs_1_out_59, save_inputs_1_out_60, save_inputs_1_out_61, save_inputs_1_out_62, save_inputs_1_out_64, save_inputs_1_out_66);
  or or_16 (or_16_out, save_inputs_1_out_63, save_inputs_1_out_65, save_inputs_1_out_67, save_inputs_1_out_68, save_inputs_1_out_69, save_inputs_1_out_70, save_inputs_1_out_71, save_inputs_1_out_73, save_inputs_1_out_75);
  or or_17 (or_17_out, save_inputs_1_out_72, save_inputs_1_out_74, save_inputs_1_out_76, save_inputs_1_out_77, save_inputs_1_out_78, save_inputs_1_out_79, save_inputs_1_out_80, save_inputs_1_out_82, save_inputs_1_out_84);
  or or_18 (or_18_out, save_inputs_1_out_81, save_inputs_1_out_83, save_inputs_1_out_85, save_inputs_1_out_86, save_inputs_1_out_87, save_inputs_1_out_88, save_inputs_1_out_89, save_inputs_1_out_90, save_inputs_1_out_91);
  display_encode_sub1 display_encode_sub1_1 (
    .in_1(or_10_out), .in_2(or_11_out), .in_3(or_12_out), .in_4(or_13_out), .in_5(or_14_out),
    .in_6(or_15_out), .in_7(or_16_out), .in_8(or_17_out), .in_9(or_18_out),
    .out_10(display_encode_sub1_1_out_10), .out_11(display_encode_sub1_1_out_11),
    .out_12(display_encode_sub1_1_out_12), .out_13(display_encode_sub1_1_out_13),
    .out_14(display_encode_sub1_1_out_14), .out_15(display_encode_sub1_1_out_15),
    .out_16(display_encode_sub1_1_out_16), .out_17(display_encode_sub1_1_out_17),
    .out_18(display_encode_sub1_1_out_18));
endmodule

module led1 (
  input  in_1,
  input  in_2,
  input  in_3,
  input  in_4,
  input  CLEAR,
  output [8:0] _3,
  output [8:0] _4,
  output [8:0] _2,
  output [8:0] _5,
  output [8:0] _1,
  output [8:0] _6,
  output [8:0] _7,
  output [8:0] _0,
  output [8:0] _8
);

  wire and_1_out, and_2_out, and_3_out, and_4_out, and_5_out, and_6_out, clock_1_out, clock_2_out, or_1_out,
       or_2_out, or_6_out, or_7_out, or_8_out, or_11_out;

  Clock clock_1 (.out(clock_1_out));
  or or_1 (or_1_out, and_2_out, _1[1]);
  D_Flip_Flop d_ff_1 (.clk(clock_1_out), .D(or_1_out), .Q(_1[1]), .reset(CLEAR));  // open: Qn, preset, en
  D_Flip_Flop d_ff_2 (.clk(clock_1_out), .D(or_2_out), .Q(_0[7]), .reset(CLEAR));  // open: Qn, preset, en
  or or_2 (or_2_out, _0[7], and_1_out);
  or or_3 (_0[0], _0[7], _1[0], _1[1]);
  and and_1 (and_1_out, in_1, in_3);
  and and_2 (and_2_out, in_3, in_2);
  or or_4 (_0[8], _1[7], _1[8], _0[7]);
  and and_3 (and_3_out, in_1, in_2);
  or or_5 (_4[4], _1[1], _1[7]);
  or or_6 (or_6_out, _1[8], and_3_out);
  and and_4 (and_4_out, in_4, in_3);
  D_Flip_Flop d_ff_3 (.clk(clock_2_out), .D(or_6_out), .Q(_1[8]), .reset(CLEAR));  // open: Qn, preset, en
  or or_7 (or_7_out, and_4_out, _1[0]);
  and and_5 (and_5_out, in_2, in_4);
  and and_6 (and_6_out, in_4, in_1);
  or or_8 (or_8_out, _8[7], and_5_out);
  D_Flip_Flop d_ff_4 (.clk(clock_2_out), .D(or_7_out), .Q(_1[0]), .reset(CLEAR));  // open: Qn, preset, en
  or or_9 (_8[8], _8[7], _1[8], _1[1]);
  D_Flip_Flop d_ff_5 (.clk(clock_2_out), .D(or_8_out), .Q(_8[7]), .reset(CLEAR));  // open: Qn, preset, en
  or or_10 (_8[0], _1[7], _1[0], _8[7]);
  or or_11 (or_11_out, and_6_out, _1[7]);
  D_Flip_Flop d_ff_6 (.clk(clock_2_out), .D(or_11_out), .Q(_1[7]), .reset(CLEAR));  // open: Qn, preset, en
  Clock clock_2 (.out(clock_2_out));

  assign _0[6:1] = {6{_0[7]}};
  assign {_2[8], _2[6], _2[2], _2[0]} = {_1[8:7], _1[1:0]};
  assign {_3[8], _3[5], _3[3], _3[0]} = {_1[8:7], _1[1:0]};
  assign {_4[8], _4[0]} = {_1[8], _1[0]};
  assign {_5[8], _5[5], _5[3], _5[0]} = {_1[8], _1[1], _1[7], _1[0]};
  assign {_6[8], _6[6], _6[2], _6[0]} = {_1[8], _1[1], _1[7], _1[0]};
  assign {_7[8:7], _7[1:0]} = {_1[8], _1[1], _1[7], _1[0]};
  assign _8[6:1] = {6{_8[7]}};
endmodule

module enable (
  input  in_1,
  input  in_2,
  input  in_3,
  input  in_4,
  input  in_5,
  input  in_6,
  input  in_7,
  input  in_8,
  input  in_9,
  input  in_10,
  output out_11,
  output out_12,
  output out_13,
  output out_14,
  output out_15,
  output out_16,
  output out_17,
  output out_18,
  output out_19
);

  and and_1 (out_11, in_2, in_1);
  and and_2 (out_12, in_3, in_1);
  and and_3 (out_13, in_4, in_1);
  and and_4 (out_14, in_5, in_1);
  and and_5 (out_15, in_6, in_1);
  and and_6 (out_16, in_7, in_1);
  and and_7 (out_17, in_8, in_1);
  and and_8 (out_18, in_9, in_1);
  and and_9 (out_19, in_10, in_1);
endmodule

module Compare (
  input  UNLOCK,
  input  RESET,
  input  RESET_CLR,
  input  in_4,
  input  in_5,
  input  in_6,
  input  in_7,
  input  in_8,
  input  in_9,
  input  in_10,
  input  in_11,
  input  in_12,
  input  NORMAL_CLR,
  output out_14
);

  wire and_1_out, stay_1_out_3;
  wire [3:0] connector_1_out_12, connector_1_out_13, connector_1_out_14, connector_1_out_15,
       connector_1_out_16, connector_1_out_17, connector_1_out_18, connector_1_out_19, connector_1_out_20,
       connector_2_out_12, connector_2_out_13, connector_2_out_14, connector_2_out_15, connector_2_out_16,
       connector_2_out_17, connector_2_out_18, connector_2_out_19, connector_2_out_20;

  and and_1 (and_1_out, RESET, stay_1_out_3);
  connector connector_1 (
    .ENABLE(and_1_out), .RESET(RESET_CLR), .in_3(in_4), .in_4(in_5), .in_5(in_6), .in_6(in_7), .in_7(in_8),
    .in_8(in_9), .in_9(in_10), .in_10(in_11), .in_11(in_12), .out_12(connector_1_out_12),
    .out_13(connector_1_out_13), .out_14(connector_1_out_14), .out_15(connector_1_out_15),
    .out_16(connector_1_out_16), .out_17(connector_1_out_17), .out_18(connector_1_out_18),
    .out_19(connector_1_out_19), .out_20(connector_1_out_20));
  connector connector_2 (
    .ENABLE(UNLOCK), .RESET(NORMAL_CLR), .in_3(in_4), .in_4(in_5), .in_5(in_6), .in_6(in_7), .in_7(in_8),
    .in_8(in_9), .in_9(in_10), .in_10(in_11), .in_11(in_12), .out_12(connector_2_out_12),
    .out_13(connector_2_out_13), .out_14(connector_2_out_14), .out_15(connector_2_out_15),
    .out_16(connector_2_out_16), .out_17(connector_2_out_17), .out_18(connector_2_out_18),
    .out_19(connector_2_out_19), .out_20(connector_2_out_20));
  stay stay_1 (.in_1(out_14), .CLEAR(NORMAL_CLR), .out_3(stay_1_out_3));
  _9_bit_compare u_9_bit_compare_1 (
    .in_1(connector_1_out_12), .in_2(connector_1_out_13), .in_3(connector_1_out_14),
    .in_4(connector_1_out_15), .in_5(connector_1_out_16), .in_6(connector_1_out_17),
    .in_7(connector_1_out_18), .in_8(connector_1_out_19), .in_9(connector_1_out_20),
    .in_10(connector_2_out_12), .in_11(connector_2_out_13), .in_12(connector_2_out_14),
    .in_13(connector_2_out_15), .in_14(connector_2_out_16), .in_15(connector_2_out_17),
    .in_16(connector_2_out_18), .in_17(connector_2_out_19), .in_18(connector_2_out_20), .out_19(out_14));
endmodule

module _9_bit_compare (
  input  [3:0] in_1,
  input  [3:0] in_2,
  input  [3:0] in_3,
  input  [3:0] in_4,
  input  [3:0] in_5,
  input  [3:0] in_6,
  input  [3:0] in_7,
  input  [3:0] in_8,
  input  [3:0] in_9,
  input  [3:0] in_10,
  input  [3:0] in_11,
  input  [3:0] in_12,
  input  [3:0] in_13,
  input  [3:0] in_14,
  input  [3:0] in_15,
  input  [3:0] in_16,
  input  [3:0] in_17,
  input  [3:0] in_18,
  output out_19
);

  wire comparator_1_eq, comparator_2_eq, comparator_3_eq, comparator_4_eq, comparator_5_eq, comparator_6_eq,
       comparator_7_eq, comparator_8_eq, comparator_9_eq;

  Comparator #(.width(4)) comparator_1 (.a(in_1), .b(in_10), .eq(comparator_1_eq));  // open: gt, lt
  Comparator #(.width(4)) comparator_2 (.a(in_2), .b(in_11), .eq(comparator_2_eq));  // open: gt, lt
  Comparator #(.width(4)) comparator_3 (.a(in_3), .b(in_12), .eq(comparator_3_eq));  // open: gt, lt
  Comparator #(.width(4)) comparator_4 (.a(in_4), .b(in_13), .eq(comparator_4_eq));  // open: gt, lt
  Comparator #(.width(4)) comparator_5 (.a(in_5), .b(in_14), .eq(comparator_5_eq));  // open: gt, lt
  Comparator #(.width(4)) comparator_6 (.a(in_6), .b(in_15), .eq(comparator_6_eq));  // open: gt, lt
  Comparator #(.width(4)) comparator_7 (.a(in_7), .b(in_16), .eq(comparator_7_eq));  // open: gt, lt
  Comparator #(.width(4)) comparator_8 (.a(in_8), .b(in_17), .eq(comparator_8_eq));  // open: gt, lt
  Comparator #(.width(4)) comparator_9 (.a(in_9), .b(in_18), .eq(comparator_9_eq));  // open: gt, lt
  and and_1 (out_19, comparator_1_eq, comparator_2_eq, comparator_3_eq, comparator_4_eq, comparator_5_eq, comparator_6_eq, comparator_7_eq, comparator_8_eq, comparator_9_eq);
endmodule

module test (
  input  in_1,
  input  in_2,
  input  in_3,
  input  in_4,
  input  in_5,
  input  in_6,
  input  in_7,
  input  in_8,
  input  in_9,
  input  in_10,
  input  in_11,
  input  in_12
);

  wire clock_1_out, enable_1_p13, enable_1_p14, enable_1_p15, undriven, undriven_2;
  wire [6:0] keyboard_1_data;

  // enable enable_1: pin names not known; wires that end beside it: in_2, in_3, in_4, in_5, in_6, in_7, in_8, in_9, in_10, in_11, in_12, in_1, enable_1_p13, enable_1_p14, enable_1_p15
  Keyboard keyboard_1 (.clk(clock_1_out), .data(keyboard_1_data));  // open: re, clr, avail
  Clock clock_1 (.out(clock_1_out));
  TTY tty_1 (.data(keyboard_1_data), .clk(clock_1_out), .we(undriven), .clr(undriven_2));
endmodule

module button (
  input  CLEAR,
  input  in_2,
  input  in_3,
  input  in_4,
  input  in_5,
  input  in_6,
  input  in_7,
  input  in_8,
  input  in_9,
  input  in_10,
  output out_11,
  output out_12,
  output out_13,
  output out_14,
  output out_15,
  output out_16,
  output out_17,
  output out_18,
  output out_19
);

  wire clock_1_out, or_1_out, or_2_out, or_3_out, or_4_out, or_5_out, or_6_out, or_7_out, or_8_out, or_9_out;

  Clock clock_1 (.out(clock_1_out));
  or or_1 (or_1_out, out_11, in_2);
  or or_2 (or_2_out, out_12, in_3);
  or or_3 (or_3_out, out_13, in_4);
  or or_4 (or_4_out, out_14, in_5);
  or or_5 (or_5_out, out_15, in_6);
  or or_6 (or_6_out, out_16, in_7);
  or or_7 (or_7_out, out_17, in_8);
  or or_8 (or_8_out, out_18, in_9);
  or or_9 (or_9_out, out_19, in_10);
  D_Flip_Flop d_ff_1 (.clk(clock_1_out), .D(or_1_out), .Q(out_11), .reset(CLEAR));  // open: Qn, preset, en
  D_Flip_Flop d_ff_2 (.clk(clock_1_out), .D(or_2_out), .Q(out_12), .reset(CLEAR));  // open: Qn, preset, en
  D_Flip_Flop d_ff_3 (.clk(clock_1_out), .D(or_3_out), .Q(out_13), .reset(CLEAR));  // open: Qn, preset, en
  D_Flip_Flop d_ff_4 (.clk(clock_1_out), .D(or_4_out), .Q(out_14), .reset(CLEAR));  // open: Qn, preset, en
  D_Flip_Flop d_ff_5 (.clk(clock_1_out), .D(or_5_out), .Q(out_15), .reset(CLEAR));  // open: Qn, preset, en
  D_Flip_Flop d_ff_6 (.clk(clock_1_out), .D(or_6_out), .Q(out_16), .reset(CLEAR));  // open: Qn, preset, en
  D_Flip_Flop d_ff_7 (.clk(clock_1_out), .D(or_7_out), .Q(out_17), .reset(CLEAR));  // open: Qn, preset, en
  D_Flip_Flop d_ff_8 (.clk(clock_1_out), .D(or_8_out), .Q(out_18), .reset(CLEAR));  // open: Qn, preset, en
  D_Flip_Flop d_ff_9 (.clk(clock_1_out), .D(or_9_out), .Q(out_19), .reset(CLEAR));  // open: Qn, preset, en
endmodule

module stay (
  input  in_1,
  input  CLEAR,
  output out_3
);

  wire clock_1_out, or_1_out;

  Clock clock_1 (.out(clock_1_out));
  or or_1 (or_1_out, out_3, in_1);
  D_Flip_Flop d_ff_1 (.clk(clock_1_out), .D(or_1_out), .Q(out_3), .reset(CLEAR));  // open: Qn, preset, en
endmodule

module letter_display_sub1 (
  output [6:0] U,
  output [6:0] N,
  output [6:0] L,
  output [6:0] O,
  output [6:0] C,
  output [6:0] K,
  output [6:0] E,
  output [6:0] D
);


  assign C = 7'b1000011;
  assign D = 7'b1000100;
  assign E = 7'b1000101;
  assign K = 7'b1001011;
  assign L = 7'b1001100;
  assign N = 7'b1001110;
  assign O = 7'b1001111;
  assign U = 7'b1010101;
endmodule

module letter_display_sub2 (
  input  MOMENTARY_IP,
  input  NORMAL_IP,
  output [6:0] out_3
);

  wire clock_1_out;
  wire [6:0] and_1_out, and_2_out, and_3_out, and_4_out, and_5_out, and_6_out, and_7_out, and_8_out,
       and_9_out, and_10_out, letter_display_sub1_1_c, letter_display_sub1_1_d, letter_display_sub1_1_e,
       letter_display_sub1_1_k, letter_display_sub1_1_l, letter_display_sub1_1_n, letter_display_sub1_1_o,
       letter_display_sub1_1_u, or_1_out, or_2_out, or_3_out, or_4_out, or_5_out, or_6_out, or_7_out,
       register_2_q, register_3_q, register_4_q, register_5_q, register_6_q, register_7_q, register_8_q;

  Clock clock_1 (.out(clock_1_out));
  letter_display_sub1 letter_display_sub1_1 (
    .U(letter_display_sub1_1_u), .N(letter_display_sub1_1_n), .L(letter_display_sub1_1_l),
    .O(letter_display_sub1_1_o), .C(letter_display_sub1_1_c), .K(letter_display_sub1_1_k),
    .E(letter_display_sub1_1_e), .D(letter_display_sub1_1_d));
  assign or_1_out = register_2_q | and_1_out;  // OR_Gate or_1, 7 bits wide
  assign and_1_out = {7{MOMENTARY_IP}} & and_2_out;  // AND_Gate and_1, 7 bits wide
  Register #(.width(7)) register_1 (.D(or_1_out), .en(1'b1), .Q(out_3), .clk(clock_1_out));  // open: clr
  assign and_2_out = letter_display_sub1_1_u & {7{NORMAL_IP}};  // AND_Gate and_2, 7 bits wide
  assign or_2_out = register_3_q | and_3_out;  // OR_Gate or_2, 7 bits wide
  Register #(.width(7)) register_2 (.D(or_2_out), .en(1'b1), .Q(register_2_q), .clk(clock_1_out));  // open: clr
  assign and_3_out = {7{MOMENTARY_IP}} & and_4_out;  // AND_Gate and_3, 7 bits wide
  assign and_4_out = letter_display_sub1_1_n & {7{NORMAL_IP}};  // AND_Gate and_4, 7 bits wide
  assign or_3_out = register_4_q | and_5_out;  // OR_Gate or_3, 7 bits wide
  assign and_5_out = {7{MOMENTARY_IP}} & letter_display_sub1_1_l;  // AND_Gate and_5, 7 bits wide
  Register #(.width(7)) register_3 (.D(or_3_out), .en(1'b1), .Q(register_3_q), .clk(clock_1_out));  // open: clr
  assign or_4_out = register_5_q | and_6_out;  // OR_Gate or_4, 7 bits wide
  Register #(.width(7)) register_4 (.D(or_4_out), .en(1'b1), .Q(register_4_q), .clk(clock_1_out));  // open: clr
  assign and_6_out = {7{MOMENTARY_IP}} & letter_display_sub1_1_o;  // AND_Gate and_6, 7 bits wide
  Register #(.width(7)) register_5 (.D(or_5_out), .en(1'b1), .Q(register_5_q), .clk(clock_1_out));  // open: clr
  assign or_5_out = register_6_q | and_7_out;  // OR_Gate or_5, 7 bits wide
  assign and_7_out = {7{MOMENTARY_IP}} & letter_display_sub1_1_c;  // AND_Gate and_7, 7 bits wide
  Register #(.width(7)) register_6 (.D(or_6_out), .Q(register_6_q), .clk(clock_1_out));  // open: en, clr
  assign or_6_out = register_7_q | and_8_out;  // OR_Gate or_6, 7 bits wide
  assign and_8_out = {7{MOMENTARY_IP}} & letter_display_sub1_1_k;  // AND_Gate and_8, 7 bits wide
  assign or_7_out = register_8_q | and_9_out;  // OR_Gate or_7, 7 bits wide
  Register #(.width(7)) register_7 (.D(or_7_out), .en(1'b1), .Q(register_7_q), .clk(clock_1_out));  // open: clr
  assign and_9_out = {7{MOMENTARY_IP}} & letter_display_sub1_1_e;  // AND_Gate and_9, 7 bits wide
  assign and_10_out = {7{MOMENTARY_IP}} & letter_display_sub1_1_d;  // AND_Gate and_10, 7 bits wide
  Register #(.width(7)) register_8 (.D(and_10_out), .en(1'b1), .Q(register_8_q), .clk(clock_1_out));  // open: clr
endmodule

module momentary (
  input  in_1,
  output out_2
);

  wire clock_1_out, d_ff_1_q;

  Clock clock_1 (.out(clock_1_out));
  D_Flip_Flop d_ff_1 (.clk(clock_1_out), .D(in_1), .Q(d_ff_1_q), .en(1'b1));  // open: Qn, preset, reset
  xor xor_1 (out_2, in_1, d_ff_1_q);
endmodule
